# Fritzing sketch photoresistor-wiring (saved by Fritzing 0.9.5d)
breadboards: 1

parts:
  Part1 = Arduino Uno (Rev3)
  R1 = PHOTOCELL [package=photocell-kit]
  LED1 = smd LED [color="Red (633nm)" package="0603 [SMD]"]
  R5 = Resistor [tolerance=±0.05% resistance=330 package=THT]
  R2 = Resistor [tolerance=±5% resistance=10k package=THT]

nets:
  N1: Part1.A0, R1.P$1, R2.Pin_0
  N2: Part1.D9_PWM, LED1.cathode
  N3: Part1.5V, R1.P$2
  N4: Part1.GND, R5.Pin_0, R2.Pin_1
  N5: LED1.anode, R5.Pin_1
