# Fritzing sketch wx-station-wiring (saved by Fritzing 0.9.5d)
breadboards: 1

parts:
  Part1 = Arduino Uno (Rev3)
  DHT1 = DHT11 Humitidy and Temperature Sensor (3 pins)
  R1 = PHOTOCELL [package=photocell-kit]
  R3 = Temperature Sensor (Thermistor) [thermistor_type=NTC package=THT]
  LED1 = smd LED [color="Red (633nm)" package="0603 [SMD]"]
  R5 = Resistor [tolerance=±0.05% resistance=330 package=THT]
  R2 = Resistor [tolerance=±5% resistance=10k package=THT]
  R4 = Resistor [tolerance=±5% resistance=10k package=THT]

nets:
  N1: Part1.A0, R1.P$1, R2.Pin_0
  N2: Part1.A1, R3.pin_0, R4.Pin_0
  N3: Part1.D9_PWM, LED1.cathode
  N4: Part1.D2, DHT1.Signal
  N5: Part1.5V, DHT1.Plus, R1.P$2, R3.pin_1
  GND: Part1.GND, DHT1.Gnd, R5.Pin_0, R2.Pin_1, R4.Pin_1
  N6: LED1.anode, R5.Pin_1

custom parts:
  DHT11 Humitidy and Temperature Sensor (3 pins): DHT11 Humidity and Temperature Sensor (3 pins).
